// Logisim project Lab5_q1.circ as structural Verilog: 1 circuit, main circuit main
module main (
  input  in_1,
  input  C_0,
  input  in_3,
  input  in_4,
  input  in_5,
  input  in_6,
  input  in_7,
  input  in_8,
  input  in_9,
  output s0,
  output C_1,
  output s1,
  output C_2,
  output s2,
  output C_3,
  output s3,
  output C_4
);

  wire and_1_out, and_2_out, and_3_out, and_4_out, and_5_out, and_6_out, and_7_out, and_8_out, and_9_out,
       and_10_out, and_11_out, and_12_out, and_13_out, and_14_out, xor_1_out, xor_2_out, xor_3_out, xor_4_out;

  and and_1 (and_1_out, in_1, in_3);
  xor xor_1 (xor_1_out, in_4, in_5);
  and and_2 (and_2_out, in_5, in_4);
  xor xor_2 (xor_2_out, in_6, in_7);
  and and_3 (and_3_out, in_6, in_7);
  xor xor_3 (xor_3_out, in_8, in_9);
  and and_4 (and_4_out, in_8, in_9);
  xor xor_4 (xor_4_out, in_1, in_3);
  xor xor_5 (s0, xor_4_out, C_0);
  and and_5 (and_5_out, C_0, xor_4_out);
  and and_6 (and_6_out, and_3_out, xor_3_out);
  or or_1 (C_1, and_5_out, and_1_out);
  and and_7 (and_7_out, and_5_out, xor_1_out);
  and and_8 (and_8_out, and_12_out, xor_3_out);
  xor xor_6 (s1, C_1, xor_1_out);
  and and_9 (and_9_out, and_7_out, xor_2_out);
  and and_10 (and_10_out, and_2_out, xor_2_out);
  and and_11 (and_11_out, and_1_out, xor_1_out);
  and and_12 (and_12_out, and_11_out, xor_2_out);
  and and_13 (and_13_out, and_9_out, xor_3_out);
  or or_2 (C_2, and_7_out, and_11_out, and_2_out);
  xor xor_7 (s2, C_2, xor_2_out);
  and and_14 (and_14_out, and_10_out, xor_3_out);
  or or_3 (C_3, and_9_out, and_12_out, and_10_out, and_3_out);
  xor xor_8 (s3, C_3, xor_3_out);
  or or_4 (C_4, and_14_out, and_13_out, and_8_out, and_6_out, and_4_out);
endmodule
